# Fritzing sketch tranmitter (saved by Fritzing 0.9.6b)
perfboards: 2

parts:
  Part1 = Arduino Pro Micro (Clone)
  U1 = SLIDER [package=slider]
  U2 = SWITCH_SPDT [package=kps-1290]
  Part2 = SparkFun LiPo Charger Booster-5V1A [part_number="PRT-14411 "]
  U3 = transmitter
  R1 = Rotary Potentiometer (Small) [maximum_resistance=100kΩ package=THT]
  S1 = Momentary Switch [package=ksa_sealed_tac_switch]
  S2 = Momentary Switch [package=ksa_sealed_tac_switch]
  S3 = Momentary Switch [package=ksa_sealed_tac_switch]
  0_91_Inch_I2C_OLED_Display1 = 0.91 Inch I2C OLED Display
  R2 = Resistor [tolerance=±5% resistance=10k package="2010 [SMD]"]
  U4 = LIPO-2000mAh [package=lipo-2000]
  R3 = Resistor [tolerance=±5% resistance=10k package="2010 [SMD]"]
  R4 = Resistor [tolerance=±5% resistance=10k package="2010 [SMD]"]

nets:
  GND: Part1.GND, U1.S, Part2.GND, U4.-
  N1: Part1.D2, 0_91_Inch_I2C_OLED_Display1.SDA
  N2: Part1.D3, 0_91_Inch_I2C_OLED_Display1.SCK
  N3: Part1.D8, S2.1
  N4: Part1.D9, S1.1
  N5: Part1.D14, U3.connector1
  N6: Part1.A0, R1.wiper
  N7: Part1.A1, U1.E
  N8: Part1.RAW, Part2.VCC
  N9: U2.O, Part2.1, U4.+
  N10: U2.P, Part2.VBATT
  N11: R1.leg2, 0_91_Inch_I2C_OLED_Display1.VCC
  N12: S1.2, R2.Pin_0
  N13: S3.2, R4.Pin_0
  N14: 0_91_Inch_I2C_OLED_Display1.GND, R3.Pin_1

custom parts:
  SparkFun LiPo Charger Booster-5V1A: The SparkFun 5V/1A LiPo Charger/Booster is a no-nonsense circuit for generating one amp from a Lithium Polymer battery at 5V. This LiPo charger is a very economical choice that is equipped with a simple booster circuit utilizing the PAM2401 IC, and includes protection diodes so you can run multiple cells in series for an extra kick. While the booster circuit is in operation, this board can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
  0.91 Inch I2C OLED Display: Strong contrast by the use of the innovative OLED technology in the wide 0.91 inch Display! Due to the high resolution of 128x32 pixels the Display offers plenty of space to Display items! Easy connection of the display with Arduino, Raspberry Pi, and co. by I2C interface only four Pins! Thanks To The Standard Controller (SSD 1306) already libraries for Arduino, Raspberry Pi, and co. exist,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
