# Fritzing sketch receiver (saved by Fritzing 0.9.6b)
perfboards: 2

parts:
  U7 = RF-LINK_RX [package=rf-link_rx]  # not connected
  Part1 = Tchauduino
  M1 = RioRand LM2596
  U9 = SWITCH-SPST-2 [package=switch-spst-vertical]
  U10 = POT [package=alps_pot]
  U11 = POT [package=alps_pot]
  J1 = Camdenboss CTB0158-3 [part_number=CTB0158-3 package=THT]
  JACK1 = 2.1mm Barrel Jack with Terminal Block
  PART1 = Sound Detector
  Q2 = Basic FET N-Channel [package="D2Pak [SMD]"]  # not connected
  LED1 = smd LED [color="Red (633nm)" package="1206 [SMD]"]
  U12 = WS2815 RGB LED strip
  U13 = WS2815 RGB LED strip
  U14 = WS2815 RGB LED strip
  U15 = WS2815 RGB LED strip
  LED2 = smd LED [color="Red (633nm)" package="1206 [SMD]"]
  LED3 = smd LED [color="Red (633nm)" package="1206 [SMD]"]
  LED4 = smd LED [color="Red (633nm)" package="1206 [SMD]"]
  LED5 = smd LED [color="Red (633nm)" package="1206 [SMD]"]
  LED6 = smd LED [color="Red (633nm)" package="1206 [SMD]"]
  J2 = Camdenboss CTB0158-4 [part_number=CTB0158-4 package=THT]

nets:
  N1: Part1.D7, U15.DOUT
  N2: Part1.D6, U14.DOUT
  N3: Part1.D5, U13.DOUT
  N4: Part1.D4, U12.DOUT
  N5: Part1.GND#92, PART1.GND
  N6: Part1.A2, U11.S
  N7: Part1.A1, U10.S
  N8: Part1.A0, PART1.ENVELOPE
  N9: Part1.5V#103, PART1.VCC
  N10: Part1.GND#104, U10.E
  N11: Part1.GND#105, U11.E
  N12: Part1.5V#106, U11.A
  N13: Part1.5V#107, U10.A
  N14: Part1.GND#108, M1.Pin_4
  N15: Part1.5V_in, M1.Pin_3
  N16: M1.Pin_1, J1.pin2
  N17: M1.Pin_2, J2.pin2
  N18: U9.O, JACK1.POS
  N19: U9.P, J1.pin1
  N20: J1.terminal_3, LED6.anode
  N21: JACK1.NEG, J2.pin1
  N22: LED1.anode, LED2.cathode
  GND: U12.GND, U13.GND, U14.GND, U15.GND, J2.pin3
  VCC: U12.VCC, U13.VCC, U14.VCC, U15.VCC
  N23: LED2.anode, LED3.cathode
  N24: LED3.anode, LED4.cathode
  N25: LED4.anode, LED5.cathode
  N26: LED5.anode, LED6.cathode

notes:
  12V
  Red diodes
  LED stripes

custom parts:
  RF-LINK_RX: RF Link receivers- WRL-8947, 8948, 8949, 8950
  Tchauduino: https://gitlab.com/bbonnal/tchauduino
  Sound Detector: Electret microphone with multiple outputs. - First output is the actual audio - Second output is the amplitude envelope - Third output is a binary "sound present" indication - high while sound is present, low otherwise. Visit sparkfun.com for more documentations.
  WS2815 RGB LED strip: WS2815 strip
